// Logisim project Project #1 - 3-bit Counter.circ as structural Verilog: 4 circuits, main circuit main
module main (
  input  X1,
  input  Y1,
  input  Cin,
  input  X2,
  input  Y2,
  input  X3,
  input  Y3,
  output out_8,
  output out_9,
  output out_10,
  output out_11
);

  wire sum_cout_1_cout, sum_cout_2_cout;

  Sum_Cout sum_cout_1 (.X(X1), .Y(Y1), .Cin(Cin), .Sum(out_8), .Cout(sum_cout_1_cout));
  Sum_Cout sum_cout_2 (.X(X2), .Y(Y2), .Cin(sum_cout_1_cout), .Sum(out_11), .Cout(sum_cout_2_cout));
  Sum_Cout sum_cout_3 (.X(X3), .Y(Y3), .Cin(sum_cout_2_cout), .Sum(out_10), .Cout(out_9));
endmodule

module Sum (
  input  X,
  input  Y,
  input  Cin,
  output Fsum
);

  wire and_1_out, and_2_out, and_3_out, and_4_out, not_1_out, not_2_out, not_3_out, not_4_out, not_5_out,
       not_6_out;

  not not_1 (not_1_out, X);
  not not_2 (not_2_out, Y);
  not not_3 (not_3_out, X);
  not not_4 (not_4_out, Cin);
  not not_5 (not_5_out, Y);
  not not_6 (not_6_out, Cin);
  and and_1 (and_1_out, not_1_out, not_2_out, Cin);
  and and_2 (and_2_out, not_3_out, Y, not_4_out);
  and and_3 (and_3_out, X, Y, Cin);
  and and_4 (and_4_out, X, not_5_out, not_6_out);
  or or_1 (Fsum, and_1_out, and_2_out, and_3_out, and_4_out);
endmodule

module Cout (
  input  X,
  input  Y,
  input  Cin,
  output out_4
);

  wire and_1_out, and_2_out, and_3_out;

  and and_1 (and_1_out, Y, Cin);
  and and_2 (and_2_out, X, Y);
  and and_3 (and_3_out, X, Cin);
  or or_1 (out_4, and_1_out, and_2_out, and_3_out);
endmodule

module Sum_Cout (
  input  X,
  input  Y,
  input  Cin,
  output Sum,
  output Cout
);

  Sum u_Sum (.X(X), .Y(Y), .Cin(Cin), .Fsum(Sum));
  Cout u_Cout (.X(X), .Y(Y), .Cin(Cin), .out_4(Cout));
endmodule
