// Logisim project Project #2 Cicuit - Daniel Williamson.circ as structural Verilog: 9 circuits, main circuit main
module main (
);

  wire bottom_1_out_5, bottomleft_1_out_5, bottomright_1_out_5, button_1_out, clock_1_out_2, clock_1_out_3,
       clock_1_out_4, clock_1_out_5, middle_1_out_5, top_1_out_5, topleft_1_out_5, topright_1_out_5;

  Button button_1 (.out(button_1_out));
  Clock clock_1 (
    .in_1(button_1_out), .out_2(clock_1_out_2), .out_3(clock_1_out_3), .out_4(clock_1_out_4),
    .out_5(clock_1_out_5));
  TopRight topright_1 (
    .A(clock_1_out_2), .B(clock_1_out_3), .C(clock_1_out_4), .D(clock_1_out_5), .out_5(topright_1_out_5));
  Top top_1 (.A(clock_1_out_2), .B(clock_1_out_3), .C(clock_1_out_4), .D(clock_1_out_5), .out_5(top_1_out_5));
  TopLeft topleft_1 (
    .A(clock_1_out_2), .B(clock_1_out_3), .C(clock_1_out_4), .D(clock_1_out_5), .out_5(topleft_1_out_5));
  Middle middle_1 (.A(clock_1_out_2), .B(clock_1_out_3), .C(clock_1_out_4), .D(clock_1_out_5), .out_5(middle_1_out_5));
  BottomLeft bottomleft_1 (
    .A(clock_1_out_2), .B(clock_1_out_3), .C(clock_1_out_4), .D(clock_1_out_5), .out_5(bottomleft_1_out_5));
  Bottom bottom_1 (.A(clock_1_out_2), .B(clock_1_out_3), .C(clock_1_out_4), .D(clock_1_out_5), .out_5(bottom_1_out_5));
  BottomRight bottomright_1 (
    .A(clock_1_out_2), .B(clock_1_out_3), .C(clock_1_out_4), .D(clock_1_out_5), .out_5(bottomright_1_out_5));
  _7_Segment_Display u_7_segment_display_1 (
    .g(middle_1_out_5), .f(topleft_1_out_5), .a(top_1_out_5), .b(topright_1_out_5), .e(bottomleft_1_out_5),
    .d(bottom_1_out_5), .c(bottomright_1_out_5), .dp(1'b1));

  // Notes on the sheet:
  //   Push me! ^
endmodule

module TopRight (
  input  A,
  input  B,
  input  C,
  input  D,
  output out_5
);

  wire D_prime_B_prime_A_prime_out, D_prime_BA_out, D_prime_C_prime_out, DC_prime_B_prime_out;

  and D_prime_C_prime (D_prime_C_prime_out, ~C, ~D);  // AND_Gate
  and D_prime_B_prime_A_prime (D_prime_B_prime_A_prime_out, ~A, ~B, ~D);  // AND_Gate
  and D_prime_BA (D_prime_BA_out, A, B, ~D);  // AND_Gate
  and DC_prime_B_prime (DC_prime_B_prime_out, ~B, ~C, D);  // AND_Gate
  or or_1 (out_5, D_prime_C_prime_out, D_prime_B_prime_A_prime_out, D_prime_BA_out, DC_prime_B_prime_out);
endmodule

module Top (
  input  A,
  input  B,
  input  C,
  input  D,
  output out_5
);

  wire D_prime_B_out, D_prime_C_prime_A_prime_out, D_prime_CA_out, DC_prime_B_prime_out;

  and D_prime_C_prime_A_prime (D_prime_C_prime_A_prime_out, ~A, ~C, ~D);  // AND_Gate
  and D_prime_B (D_prime_B_out, B, ~D);  // AND_Gate
  and D_prime_CA (D_prime_CA_out, A, C, ~D);  // AND_Gate
  and DC_prime_B_prime (DC_prime_B_prime_out, ~B, ~C, D);  // AND_Gate
  or or_1 (out_5, D_prime_C_prime_A_prime_out, D_prime_B_out, D_prime_CA_out, DC_prime_B_prime_out);
endmodule

module TopLeft (
  input  A,
  input  B,
  input  C,
  input  D,
  output out_5
);

  wire D_prime_B_prime_A_prime_out, D_prime_CA_prime_out, D_prime_CB_prime_out, DC_prime_B_prime_out;

  and D_prime_B_prime_A_prime (D_prime_B_prime_A_prime_out, ~A, ~B, ~D);  // AND_Gate
  and D_prime_CB_prime (D_prime_CB_prime_out, ~B, C, ~D);  // AND_Gate
  and D_prime_CA_prime (D_prime_CA_prime_out, ~A, C, ~D);  // AND_Gate
  and DC_prime_B_prime (DC_prime_B_prime_out, ~B, ~C, D);  // AND_Gate
  or or_1 (out_5, D_prime_B_prime_A_prime_out, D_prime_CB_prime_out, D_prime_CA_prime_out, DC_prime_B_prime_out);
endmodule

module Middle (
  input  A,
  input  B,
  input  C,
  input  D,
  output out_5
);

  wire D_prime_BA_prime_out, D_prime_C_prime_B_out, D_prime_CB_prime_out, DC_prime_B_prime_out;

  and D_prime_C_prime_B (D_prime_C_prime_B_out, B, ~C, ~D);  // AND_Gate
  and D_prime_BA_prime (D_prime_BA_prime_out, ~A, B, ~D);  // AND_Gate
  and D_prime_CB_prime (D_prime_CB_prime_out, ~B, C, ~D);  // AND_Gate
  and DC_prime_B_prime (DC_prime_B_prime_out, ~B, ~C, D);  // AND_Gate
  or or_1 (out_5, D_prime_C_prime_B_out, D_prime_BA_prime_out, D_prime_CB_prime_out, DC_prime_B_prime_out);
endmodule

module BottomLeft (
  input  A,
  input  B,
  input  C,
  input  D,
  output out_5
);

  wire C_prime_B_prime_A_prime_out, D_prime_BA_prime_out;

  and D_prime_BA_prime (D_prime_BA_prime_out, ~A, B, ~D);  // AND_Gate
  and C_prime_B_prime_A_prime (C_prime_B_prime_A_prime_out, ~A, ~B, ~C);  // AND_Gate
  or or_1 (out_5, D_prime_BA_prime_out, C_prime_B_prime_A_prime_out);
endmodule

module Bottom (
  input  A,
  input  B,
  input  C,
  input  D,
  output out_5
);

  wire C_prime_B_prime_A_prime_out, D_prime_BA_prime_out, D_prime_C_prime_B_out, D_prime_CB_prime_A_out;

  and C_prime_B_prime_A_prime (C_prime_B_prime_A_prime_out, ~A, ~B, ~C);  // AND_Gate
  and D_prime_BA_prime (D_prime_BA_prime_out, ~A, B, ~D);  // AND_Gate
  and D_prime_C_prime_B (D_prime_C_prime_B_out, B, ~C, ~D);  // AND_Gate
  and D_prime_CB_prime_A (D_prime_CB_prime_A_out, A, ~B, C, ~D);  // AND_Gate
  or or_1 (out_5, C_prime_B_prime_A_prime_out, D_prime_BA_prime_out, D_prime_C_prime_B_out, D_prime_CB_prime_A_out);
endmodule

module BottomRight (
  input  A,
  input  B,
  input  C,
  input  D,
  output out_5
);

  wire C_prime_B_prime_out, D_prime_BA_out, D_prime_C_out;

  and C_prime_B_prime (C_prime_B_prime_out, ~B, ~C);  // AND_Gate
  and D_prime_C (D_prime_C_out, C, ~D);  // AND_Gate
  and D_prime_BA (D_prime_BA_out, A, B, ~D);  // AND_Gate
  or or_1 (out_5, C_prime_B_prime_out, D_prime_C_out, D_prime_BA_out);
endmodule

module Clock (
  input  in_1,
  output out_2,
  output out_3,
  output out_4,
  output out_5
);

  wire and_1_out, and_2_out, and_3_out, and_4_out, not_1_out, not_2_out;

  and and_1 (and_1_out, 1'b1, out_2);
  and and_2 (and_2_out, and_1_out, out_3);
  and and_3 (and_3_out, and_2_out, out_4);
  J_K_Flip_Flop j_k_ff_1 (.J(1'b1), .clk(in_1), .K(1'b1), .Q(out_2), .reset(and_4_out));  // open: Qn, preset, en
  J_K_Flip_Flop j_k_ff_2 (
    .J(and_1_out), .clk(in_1), .K(and_1_out), .Q(out_3), .reset(and_4_out));  // open: Qn, preset, en
  J_K_Flip_Flop j_k_ff_3 (
    .J(and_2_out), .clk(in_1), .K(and_2_out), .Q(out_4), .reset(and_4_out));  // open: Qn, preset, en
  J_K_Flip_Flop j_k_ff_4 (
    .J(and_3_out), .clk(in_1), .K(and_3_out), .Q(out_5), .reset(and_4_out));  // open: Qn, preset, en
  and and_4 (and_4_out, not_2_out, out_3, not_1_out, out_5);
  not not_1 (not_1_out, out_4);
  not not_2 (not_2_out, out_2);
endmodule
